# Fritzing sketch Schema montage (saved by Fritzing 1.0.1rc)
breadboards: 2

parts:
  LCM1602_IIC2 = LCM1602 IIC [part_number="LCM1602 IIC" chip_label="LCM1602 IIC" package="DIP (Dual Inline) [THT]"]
  Mod3 = Raspberry Pi 4B
  SEN2 = US-100 Ultrasonic Distance Sensor
  IC2 = L293D [package=THT]
  LCD2 = LCD screen
  Mod4 = Passive Buzzer
  M6 = DC Motor [voltage_(max)=6V voltage_(min)=3V]
  M7 = DC Motor [voltage_(max)=6V voltage_(min)=3V]
  VCC1 = Battery
  LED3 = smd LED [color="Red (633nm)" package="1206 [SMD]"]
  Grove1 = Grove Light Sensor
  Grove2 = Grove Light Sensor
  Grove3 = Grove Light Sensor
  Grove4 = Grove Light Sensor

nets:
  VSS: LCM1602_IIC2.VSS, LCD2.VSS
  VDD: LCM1602_IIC2.VDD, LCD2.VDD
  N1: LCM1602_IIC2.V0, LCD2.V0
  N2: LCM1602_IIC2.RS, LCD2.RS
  N3: LCM1602_IIC2.RW, LCD2.R/W
  N4: LCM1602_IIC2.E, LCD2.E
  N5: LCM1602_IIC2.D0, LCD2.DB0
  N6: LCM1602_IIC2.D1, LCD2.DB1
  N7: LCM1602_IIC2.D2, LCD2.DB2
  N8: LCM1602_IIC2.D3, LCD2.DB3
  N9: LCM1602_IIC2.D4, LCD2.DB4
  N10: LCM1602_IIC2.D5, LCD2.DB5
  N11: LCM1602_IIC2.D6, LCD2.DB6
  N12: LCM1602_IIC2.D7, LCD2.DB7
  N13: LCM1602_IIC2.A, LCD2.LED+
  N14: LCM1602_IIC2.K, LCD2.LED-
  GND: LCM1602_IIC2.GND, SEN2.GND, SEN2.GND-2, Mod4.-, LED3.cathode
  VCC: LCM1602_IIC2.VCC, Mod3.5V, IC2.+V
  N15: LCM1602_IIC2.SDA, Mod3.GPIO2
  N16: LCM1602_IIC2.SCL, Mod3.GPIO3
  VCC_2: Mod3.3V3, Mod3.GPIO9, SEN2.VCC, IC2.In_4, Grove1.VCC, Grove2.VCC, Grove3.VCC, Grove4.VCC
  N17: Mod3.GPIO4, IC2.In_1
  N18: Mod3.GPIO17, IC2.In_2
  N19: Mod3.GPIO27, IC2.In_3
  N20: Mod3.GPIO23, SEN2.ECHO
  N21: Mod3.GPIO24, SEN2.TRIG
  N22: Mod3.GPIO7, LED3.anode
  N23: Mod3.GPIO5, Grove4.SIG
  N24: Mod3.GPIO6, Grove2.SIG
  N25: Mod3.GPIO12, IC2.Enable_2
  N26: Mod3.GPIO13, Grove3.SIG
  N27: Mod3.GPIO19, IC2.Enable_1
  N28: Mod3.GPIO26, Grove1.SIG
  N29: Mod3.GPIO21, Mod4.S
  N30: IC2.Out_1_(_Controlled_by_Enable_1_), M6.pin_2
  N31: IC2.Out_2_(_Controlled_by_Enable_1_), M6.pin_1
  N32: IC2.+Vmotor, VCC1.+
  N33: IC2.Out_3_(_Controlled_by_Enable_2_), M7.pin_1
  N34: IC2.Out_4_(_Controlled_by_Enable_2_), M7.pin_2
  GND_2: Grove1.GND, Grove2.GND, Grove3.GND, Grove4.GND

custom parts:
  LCM1602 IIC: I2C-Module to use a 1602 or 2004 LCD on with the wire.h libory Serial LCD Modul
